// Logisim project GCore.circ as structural Verilog: 11 circuits, main circuit main
module main (
  input  rst,
  input  clk,
  input  out_sel,
  output [7:0] led
);

  wire alu_1_zero, and_1_out, clk_in_test_1_out, clock_1_accclk, clock_1_aluclk, clock_1_memclk,
       clock_1_opramclk, clock_1_out_clk, clock_1_pcclk, control_1_accwrite, control_1_branch,
       control_1_jump, control_1_memread, control_1_memwrite, or_1_out;
  wire [1:0] control_1_accdst;
  wire [2:0] control_1_aluop;
  wire [7:0] alu_1_ans, bit_extender_1_out, mem_control_1_data, mux_1_out, opram_control_1_op, pc_1_addr,
       shifter_1_out, undriven;

  pc pc_1 (.jumpaddr(mem_control_1_data), .jump(or_1_out), .clk(clock_1_pcclk), .rst(rst), .addr(pc_1_addr));
  clock clock_1 (
    .clock(clk_in_test_1_out), .pcclk(clock_1_pcclk), .opramclk(clock_1_opramclk), .memclk(clock_1_memclk),
    .aluclk(clock_1_aluclk), .accclk(clock_1_accclk), .out_clk(clock_1_out_clk));
  clk_in_test clk_in_test_1 (.in(clk), .out(clk_in_test_1_out));
  opram_control opram_control_1 (
    .addr(pc_1_addr), .writeop({8{1'b0}}), .write(1'b0), .read(1'b1), .clk(clock_1_opramclk), .rst(rst),
    .op(opram_control_1_op));
  or or_1 (or_1_out, and_1_out, control_1_jump);
  control control_1 (
    .op(opram_control_1_op[7:4]), .aluop(control_1_aluop), .accdst(control_1_accdst), .jump(control_1_jump),
    .branch(control_1_branch), .accwrite(control_1_accwrite), .memread(control_1_memread),
    .memwrite(control_1_memwrite));
  mem_control mem_control_1 (
    .addr(opram_control_1_op[3:0]), .writedata(undriven), .write(control_1_memwrite),
    .read(control_1_memread), .clk(clock_1_memclk), .rst(rst), .data(mem_control_1_data));
  assign bit_extender_1_out = {{4{1'b0}}, opram_control_1_op[3:0]};  // Bit_Extender bit_extender_1
  and and_1 (and_1_out, alu_1_zero, control_1_branch);
  mux mux_1 (
    .a(mem_control_1_data), .b(bit_extender_1_out), .c(shifter_1_out), .d(alu_1_ans), .sel(control_1_accdst),
    .out(mux_1_out));
  accum accum_1 (.writedata(mux_1_out), .write(control_1_accwrite), .clk(clock_1_accclk), .rst(rst), .data(undriven));
  Shifter shifter_1 (.in(undriven), .\dist (3'b100), .out(shifter_1_out));
  alu alu_1 (
    .b(mem_control_1_data), .a(undriven), .aluop(control_1_aluop), .clk(clock_1_aluclk), .zero(alu_1_zero),
    .ans(alu_1_ans));
  led_out led_out_1 (.addr(pc_1_addr), .acc(undriven), .sel(out_sel), .out(led), .clk(clock_1_out_clk));

  // Notes on the sheet:
  //   pc
  //   clk
  //   in
  //   test
  //   opaddr
  //   clock
  //   jumpaddr
  //   opram
  //   op
  //   control
  //   4-7
  //   control
  //   0-3
  //   mem
  //   control
  //   jump
  //   mux
  //   branch
  //   accum
  //   zero
  //   alu
  //   ans
  //   led
  //   out
endmodule

module pc (
  input  [7:0] jumpaddr,
  input  jump,
  input  clk,
  input  rst,
  output [7:0] addr
);

  wire [7:0] adder_1_out, multiplexer_1_out;

  Adder adder_1 (.a(addr), .b(8'h1), .out(adder_1_out));  // open: cin, cout
  Multiplexer #(.width(8), .enable("false")) multiplexer_1 (
    .in0(adder_1_out), .in1(jumpaddr), .out(multiplexer_1_out), .sel(jump));
  Register Mem (.D(multiplexer_1_out), .en(1'b1), .Q(addr), .clk(clk), .clr(rst));
endmodule

module mem_control (
  input  [3:0] addr,
  input  [7:0] writedata,
  input  write,
  input  read,
  input  clk,
  input  rst,
  output [7:0] data
);

  RAM #(.addrWidth(4), .bus("separate")) ram_1 (
    .addr(addr), .din(writedata), .data(data), .str(write), .sel(1'b1), .clk(clk), .ld(read), .clr(rst));
endmodule

module opram_control (
  input  [7:0] addr,
  input  [7:0] writeop,
  input  write,
  input  read,
  input  clk,
  input  rst,
  output [7:0] op
);

  wire and_1_out, not_1_out;

  not not_1 (not_1_out, write);
  and and_1 (and_1_out, not_1_out, read);
  RAM #(.bus("separate")) ram_1 (
    .addr(addr), .din(writeop), .data(op), .str(write), .sel(1'b1), .clk(clk), .ld(and_1_out), .clr(rst));
endmodule

module mux (
  input  [7:0] a,
  input  [7:0] b,
  input  [7:0] c,
  input  [7:0] d,
  input  [1:0] sel,
  output [7:0] out
);

  Multiplexer #(.select(2), .width(8), .enable("false")) multiplexer_1 (
    .in0(a), .in1(b), .in2(c), .in3(d), .out(out), .sel(sel));
endmodule

module accum (
  input  [7:0] writedata,
  input  [7:0] data,
  input  write,
  input  clk,
  input  rst
);

  wire [7:0] Mem_q, multiplexer_1_out, multiplexer_2_out;

  Multiplexer #(.width(8), .enable("false")) multiplexer_1 (
    .in0(Mem_q), .in1(writedata), .out(multiplexer_1_out), .sel(write));
  Multiplexer #(.width(8), .enable("false")) multiplexer_2 (
    .in0(multiplexer_1_out), .in1({8{1'b0}}), .out(multiplexer_2_out), .sel(rst));
  Register Mem (.D(multiplexer_2_out), .en(1'b1), .Q(Mem_q), .clk(clk), .clr(1'b0));
  assign data = Mem_q;  // Buffer buffer_1, 8 bits wide
endmodule

module alu (
  input  [7:0] b,
  input  [7:0] a,
  input  [2:0] aluop,
  input  clk,
  output zero,
  output [7:0] ans
);

  wire [0:0] comparator_1_lt, comparator_2_eq;
  wire [7:0] adder_1_out, and_1_out, multiplexer_1_out, or_1_out, subtractor_1_out, xor_1_out;

  Adder adder_1 (.a(a), .b(b), .out(adder_1_out));  // open: cin, cout
  Subtractor subtractor_1 (.a(a), .b(b), .out(subtractor_1_out));  // open: bin, bout
  assign and_1_out = a & b;  // AND_Gate and_1, 8 bits wide
  assign or_1_out = a | b;  // OR_Gate or_1, 8 bits wide
  assign xor_1_out = a ^ b;  // XOR_Gate xor_1, 8 bits wide
  Comparator comparator_1 (.a(a), .b(b), .lt(comparator_1_lt[0]));  // open: gt, eq
  Comparator comparator_2 (.a(a), .b(b), .eq(comparator_2_eq[0]));  // open: gt, lt
  Multiplexer #(.select(3), .width(8), .enable("false")) multiplexer_1 (
    .in0(adder_1_out), .in1(subtractor_1_out), .in2(and_1_out), .in3(or_1_out), .in4(xor_1_out),
    .in5({8{1'b0}}), .in6({{7{1'b0}}, comparator_1_lt[0]}), .in7({{7{1'b0}}, comparator_2_eq[0]}),
    .out(multiplexer_1_out), .sel(aluop));
  Register Mem (.D(multiplexer_1_out), .en(1'b1), .Q(ans), .clk(clk), .clr(1'b0));

  assign zero = ans[0];
endmodule

module control (
  input  [3:0] op,
  output [2:0] aluop,
  output [1:0] accdst,
  output jump,
  output branch,
  output accwrite,
  output memread,
  output memwrite
);

  wire comparator_1_eq;

  Comparator #(.width(4), .mode("unsigned")) comparator_1 (.a(op), .b(4'b1111), .eq(comparator_1_eq));  // open: gt, lt
  Transistor #(.width(3)) transistor_1 (.in(op[3:1]), .out(aluop), .gate(op[0]));

  assign accdst = 2'b00;
  assign accwrite = op[0];
  assign branch = op[0];
  assign jump = op[0];
  assign memread = op[0];
  assign memwrite = op[0];
endmodule

module clock (
  input  clock,
  output pcclk,
  output opramclk,
  output memclk,
  output aluclk,
  output accclk,
  output out_clk
);


  assign accclk = clock;
  assign aluclk = clock;
  assign memclk = clock;
  assign opramclk = clock;
  assign out_clk = clock;
  assign pcclk = clock;
endmodule

module clk_in_test (
  input  in,
  output out
);

  wire comparator_1_gt;
  wire [23:0] counter_1_q;

  Counter #(.width(24), .max('hffffff)) counter_1 (
    .count(1'b1), .Q(counter_1_q), .clk(in), .clr(comparator_1_gt));  // open: load, D, carry
  Comparator #(.width(24)) comparator_1 (.a(counter_1_q), .b(24'h5d8b80), .gt(comparator_1_gt), .eq(out));  // open: lt
endmodule

module led_out (
  input  [7:0] addr,
  input  [7:0] acc,
  input  sel,
  input  clk,
  output [7:0] out
);

  wire [7:0] multiplexer_1_out;

  Multiplexer #(.width(8), .enable("false")) multiplexer_1 (.in0(addr), .in1(acc), .out(multiplexer_1_out), .sel(sel));
  Transistor #(.gate("br"), .width(8)) transistor_1 (.in(multiplexer_1_out), .out(out), .gate(clk));
endmodule
